# Fritzing sketch minisumo LLSR (saved by Fritzing 0.9.3b)
perfboards: 1

parts:
  LLSB = Header 6 [package=1x06-smd-female-v2]
  LED1 = LED - 5mm [color="Red (633nm)" package="5 mm [THT]"]
  LED2 = LED - 5mm [color="Green (555nm)" package="5 mm [THT]"]
  S1 = Pushbutton [package="[THT]"]
  R1 = Resistor [tolerance=±5% resistance=220 package="1206 [SMD]"]
  gold_piny = Header 3 [package=molex-1x3_lock]

nets:
  N1: LLSB.1, LED1.anode
  N2: LLSB.2, LED2.anode
  N3: LLSB.3, gold_piny.1
  GND: LLSB.4, S1.Pin_3, S1.Pin_4, R1.Pin_0, gold_piny.2
  5V: LLSB.5, gold_piny.3
  N4: LLSB.6, S1.Pin_1, S1.Pin_2
  N5: LED1.cathode, LED2.cathode, R1.Pin_1
