# Fritzing sketch minisumo kopia (saved by Fritzing 0.9.3b)
perfboards: 1

parts:
  Part1 = Arduino Nano (Rev3.0) (ICSP)
  Part2 = Motor Driver 1A Dual TB6612FNG
  C2 = Electrolytic Capacitor [capacitance=10pF package="100 mil [THT, electrolytic]"]
  C1 = Electrolytic Capacitor [capacitance=100nF voltage=16V package="200 mil [THT, electrolytic]"]
  sensor_board = Header 6 [package=1x06-smd-female-v2]
  stabilizator = Header 3 [package=molex-1x3_lock]
  LLSB = Header 6 [package=1x06-smd-female-v2]
  U5 = SWITCH_SPDT [package=kps-1290]
  gold_piny_baterii = Header 2 [package=molex-1x2_lock]
  M1 = DC Motor
  M2 = DC Motor

nets:
  GND: Part1.GND, Part2.GND, C2.-, C1.-, sensor_board.1, stabilizator.2, LLSB.4, gold_piny_baterii.2
  N1: Part1.D2, LLSB.6
  N2: Part1.D3, Part2.PWMA
  N3: Part1.D4, Part2.AIN2
  N4: Part1.D5, Part2.AIN1
  N5: Part1.D6, LLSB.3
  N6: Part1.D7, Part2.BIN1
  N7: Part1.D8, Part2.BIN2
  N8: Part1.D9, Part2.PWMB
  N9: Part1.D10, LLSB.2
  N10: Part1.D11/MOSI, LLSB.1
  5V: Part1.5V, Part2.VCC, Part2.STBY, C2.+, sensor_board.2, stabilizator.3, LLSB.5
  N11: Part1.A7, sensor_board.3
  N12: Part1.A6, sensor_board.4
  N13: Part1.A5, sensor_board.5
  N14: Part1.A4, sensor_board.6
  N15: Part2.B01, M2.pin_2
  N16: Part2.B02, M2.pin_1
  N17: Part2.A02, M1.pin_1
  N18: Part2.A01, M1.pin_2
  N19: Part2.VM, stabilizator.1, U5.O
  N20: C1.+, U5.P, U5.S, gold_piny_baterii.1
