# Fritzing sketch sensor board (saved by Fritzing 0.9.3b)
perfboards: 3

parts:
  J1 = Infrared Proximity Sensor
  J2 = Infrared Proximity Sensor
  R5 = Resistor [tolerance=±5% resistance=10k package="2512 [SMD]"]
  R6 = Resistor [tolerance=±5% resistance=220 package="2512 [SMD]"]
  R7 = Resistor [tolerance=±5% resistance=10k package="2512 [SMD]"]
  R8 = Resistor [tolerance=±5% resistance=220 package="2512 [SMD]"]
  LED1 = smd LED [color="Blue (470nm)" package="1206 [SMD]"]
  Odbiornik1 = smd LED [color="Infrared (850nm)" package="1206 [SMD]"]
  JP3 = Header 6 [package=molex-1x6-ra_lock]
  LED2 = smd LED [color="Blue (470nm)" package="1206 [SMD]"]  # not connected
  Odbiornik2 = smd LED [color="Infrared (850nm)" package="1206 [SMD]"]  # not connected

nets:
  N1: J1.Vout, JP3.1
  GND: J1.GND, J2.GND, LED1.cathode, Odbiornik1.cathode, JP3.6
  5V: J1.Vcc, J2.Vcc, R5.Pin_0, R6.Pin_0, R7.Pin_0, R8.Pin_0, JP3.5
  N2: J2.Vout, JP3.3
  N3: R5.Pin_1, Odbiornik1.anode, JP3.2
  N4: R6.Pin_1, LED1.anode
  N5: R7.Pin_1, JP3.4
